# Fritzing sketch NRF24L01_Reciever (saved by Fritzing 0.9.6b)

parts:
  M1 = RioRand LM2596
  Part1 = NRF24L01+ Breakout Board
  Part2 = Arduino Pro Mini (5V)
  LCD1 = LCD screen
  Power_plug1 = Power plug
  R1 = Resistor [tolerance=±5% power=0.25 resistance=220 package=THT]
  R2 = Resistor [tolerance=±5% power=0.25 resistance=220 package=THT]
  R3 = Resistor [tolerance=±5% power=0.25 resistance=220 package=THT]
  R4 = Resistor [tolerance=±5% power=0.25 resistance=220 package=THT]
  LED1 = LED - 5mm [color="Red (633nm)" current=0.030 package="5 mm [THT]"]
  LED2 = LED - 5mm [color="Blue (470nm)" current=0.030 package="5 mm [THT]"]
  LED3 = LED - 5mm [color="White (4500K)" current=0.030 package="5 mm [THT]"]
  LED4 = smd LED [color="Green (570nm)" current=30mA package="0603 [SMD]"]
  J1 = Camdenboss CTB0158-2 [part_number=CTB0158-2 package=THT]
  SPKR1 = Loudspeaker
  Part3 = OpAmp Breakout
  VCC2 = 4 x AAA Battery Mount
  M2 = RioRand LM2596

nets:
  N1: M1.Pin_1, Power_plug1.VCC
  N2: M1.Pin_2, Power_plug1.GND
  N3: M1.Pin_3, Part2.VCC
  N4: M1.Pin_4, Part2.GND
  N5: Part1.CE, Part2.D9
  N6: Part1.CS, Part2.D10
  N7: Part1.SCK, Part2.SCK
  N8: Part1.MOSI, Part2.MOSI
  N9: Part1.MISO, Part2.MISO
  N10: Part2.A4, LCD1.RS
  N11: Part2.A5, LCD1.V0
  N12: Part2.D5, R3.Pin_0
  N13: Part2.D4, R2.Pin_0
  N14: Part2.D2, R4.Pin_0
  N15: R1.Pin_1, LED2.anode
  N16: R2.Pin_1, LED4.anode
  N17: R3.Pin_1, LED3.anode
  N18: R4.Pin_1, LED1.anode
  N19: J1.terminal_2, Part3.IN
  N20: SPKR1.pin2, Part3.OUT
  N21: Part3.VCC, M2.Pin_3
  N22: Part3.GND, M2.Pin_4
  N23: VCC2.-, M2.Pin_2
  N24: VCC2.+, M2.Pin_1

notes:
  Buck Converter
  15W amplifier
  Speaker / Horn
  Output Noise
  12v In Power port
  4S 1P Li-ion 18650
  LCD I2C 20x4
  Arduino Pro Mini 5v
  NRF24L01+PA/LNA
  LED indicator
