# Fritzing sketch NRF@$_Transmitter (saved by Fritzing 0.9.6b)

parts:
  M3 = RioRand LM2596
  Part4 = NRF24L01+ Breakout Board
  Part5 = Arduino Pro Mini (5V)
  LCD2 = LCD screen
  Power_plug2 = Power plug
  R5 = Resistor [tolerance=±5% power=0.25 resistance=220 package=THT]
  R6 = Resistor [tolerance=±5% power=0.25 resistance=220 package=THT]
  R7 = Resistor [tolerance=±5% power=0.25 resistance=220 package=THT]
  R8 = Resistor [tolerance=±5% power=0.25 resistance=220 package=THT]
  LED5 = LED - 5mm [color="Red (633nm)" current=0.030 package="5 mm [THT]"]  # not connected
  LED6 = LED - 5mm [color="Blue (470nm)" current=0.030 package="5 mm [THT]"]  # not connected
  LED7 = LED - 5mm [color="White (4500K)" current=0.030 package="5 mm [THT]"]  # not connected
  LED8 = smd LED [color="Green (570nm)" current=30mA package="0603 [SMD]"]  # not connected
  VCC3 = 4 x AAA Battery Mount  # not connected
  Q1 = NPN-Transistor [package="TO92 [THT]"]
  Q2 = NPN-Transistor [package="TO92 [THT]"]
  Q3 = NPN-Transistor [package="TO92 [THT]"]
  Q4 = NPN-Transistor [package="TO92 [THT]"]
  J3 = Camdenboss CTB0158-2 [part_number=CTB0158-2 package=THT]
  J4 = Camdenboss CTB0158-2 [part_number=CTB0158-2 package=THT]
  J5 = Camdenboss CTB0158-2 [part_number=CTB0158-2 package=THT]
  J6 = Camdenboss CTB0158-2 [part_number=CTB0158-2 package=THT]
  R9 = Resistor [tolerance=±5% power=0.25 resistance=220 package=THT]
  R10 = Resistor [tolerance=±5% power=0.25 resistance=220 package=THT]
  R11 = Resistor [tolerance=±5% power=0.25 resistance=220 package=THT]
  R12 = Resistor [tolerance=±5% power=0.25 resistance=220 package=THT]
  J7 = Camdenboss CTB0158-2 [part_number=CTB0158-2 package=THT]  # not connected

nets:
  N1: M3.Pin_1, Power_plug2.VCC
  N2: M3.Pin_2, Power_plug2.GND
  N3: M3.Pin_3, Part5.VCC
  N4: M3.Pin_4, Part5.GND
  N5: Part4.CE, Part5.D9
  N6: Part4.CS, Part5.D10
  N7: Part4.SCK, Part5.SCK
  N8: Part4.MOSI, Part5.MOSI
  N9: Part4.MISO, Part5.MISO
  N10: Part5.A4, LCD2.RS
  N11: Part5.A5, LCD2.V0
  N12: Part5.D5, R7.Pin_0
  N13: Part5.D4, R6.Pin_0
  N14: Part5.D3, R5.Pin_0
  N15: Part5.D2, R8.Pin_0
  N16: R5.Pin_1, Q3.E
  N17: R6.Pin_1, Q4.E
  N18: R7.Pin_1, Q1.E
  N19: R8.Pin_1, Q2.E
  N20: J3.pin2, R11.Pin_1
  N21: J4.pin2, R12.Pin_1
  N22: J5.pin2, R10.Pin_1
  N23: J6.pin2, R9.Pin_1

notes:
  Buck Converter
  12v In Power port
  4S 1P Li-ion 18650
  LCD I2C 20x4
  Arduino Pro Mini 5v
  NRF24L01+PA/LNA
  Water Level Sensor Array
